// Logisim project 22TO3.circ as structural Verilog: 1 circuit, main circuit main
module main (
  output [4:0] out_1
);

  wire and_1_out, clock_1_out, j_k_ff_1_qn, j_k_ff_2_qn, j_k_ff_3_qn, j_k_ff_4_qn;
  wire [3:0] divider_1_out;
  wire [7:0] divider_1_rem;
  wire [7:4] divider_1_out_2;

  Clock clock_1 (.out(clock_1_out));
  and and_1 (and_1_out, ~out_1[0], out_1[1], ~out_1[2], ~out_1[3], ~out_1[4]);  // AND_Gate
  J_K_Flip_Flop #(.trigger("falling")) j_k_ff_1 (
    .J(1'b1), .clk(clock_1_out), .K(1'b1), .Q(out_1[0]), .Qn(j_k_ff_1_qn), .reset(and_1_out));  // open: preset, en
  J_K_Flip_Flop #(.trigger("falling")) j_k_ff_2 (
    .J(1'b1), .clk(j_k_ff_1_qn), .K(1'b1), .Q(out_1[1]), .Qn(j_k_ff_2_qn), .preset(and_1_out));  // open: en, reset
  J_K_Flip_Flop #(.trigger("falling")) j_k_ff_3 (
    .J(1'b1), .clk(j_k_ff_2_qn), .K(1'b1), .Q(out_1[2]), .Qn(j_k_ff_3_qn), .preset(and_1_out));  // open: en, reset
  J_K_Flip_Flop #(.trigger("falling")) j_k_ff_4 (
    .J(1'b1), .clk(j_k_ff_3_qn), .K(1'b1), .Q(out_1[3]), .Qn(j_k_ff_4_qn), .reset(and_1_out));  // open: preset, en
  J_K_Flip_Flop #(.trigger("falling")) j_k_ff_5 (
    .J(1'b1), .clk(j_k_ff_4_qn), .K(1'b1), .Q(out_1[4]), .preset(and_1_out));  // open: Qn, en, reset
  Hex_Digit_Display hex_digit_display_1 (.value(divider_1_out));  // open: dp
  Hex_Digit_Display hex_digit_display_2 (.value(divider_1_rem[3:0]));  // open: dp
  Divider divider_1 (
    .a({3'b000, out_1}), .b(8'ha), .out({divider_1_out_2, divider_1_out}), .rem(divider_1_rem));  // open: upper
endmodule
