// Logisim project ARITIMETICOS.circ as structural Verilog: 3 circuits, main circuit noCout
module noCout (
  input  A,
  input  B,
  input  C,
  output S
);

  wire xor_1_out;

  xor xor_1 (xor_1_out, C, B);
  xor xor_2 (S, xor_1_out, A);

  // Notes on the sheet:
  //   A ⊗ B ⊗ C
endmodule

module Somador (
  input  in_1,
  input  [7:0] in_2,
  input  [7:0] in_3,
  output [7:0] out_4,
  output out_5
);

  wire and_1_out, and_2_out, and_3_out, and_4_out, and_5_out, and_6_out, and_7_out, and_8_out, and_9_out,
       and_10_out, and_11_out, and_12_out, and_13_out, and_14_out, and_15_out, and_16_out, and_17_out,
       and_18_out, and_19_out, and_20_out, and_21_out, and_22_out, and_23_out, and_24_out, and_25_out,
       and_26_out, and_27_out, and_28_out, G1_2_out, G1_out, G2_out, G3_out, G4_out, G5_out, G6_out, G7_out,
       or_1_out, or_2_out, or_3_out, or_4_out, or_5_out, or_6_out, or_7_out, P1_2_out, P1_out, P2_out,
       P3_out, P4_out, P5_out, P6_out, P7_out;
  wire [3:0] divider_1_out, divider_2_out, divider_3_out;
  wire [7:0] divider_1_rem, divider_2_rem, divider_3_rem, xor_1_out;
  wire [7:4] divider_1_out_2, divider_2_out_2, divider_3_out_2;

  Hex_Digit_Display hex_digit_display_1 (.value(divider_1_out));  // open: dp
  Hex_Digit_Display hex_digit_display_2 (.value(divider_2_out));  // open: dp
  Hex_Digit_Display hex_digit_display_3 (.value(divider_3_out));  // open: dp
  Hex_Digit_Display hex_digit_display_4 (.value(divider_1_rem[3:0]));  // open: dp
  Divider divider_1 (.a(in_2), .b(8'ha), .out({divider_1_out_2, divider_1_out}), .rem(divider_1_rem));  // open: upper
  Hex_Digit_Display hex_digit_display_5 (.value(divider_2_rem[3:0]));  // open: dp
  Divider divider_2 (.a(in_3), .b(8'ha), .out({divider_2_out_2, divider_2_out}), .rem(divider_2_rem));  // open: upper
  Hex_Digit_Display hex_digit_display_6 (.value(divider_3_rem[3:0]));  // open: dp
  Divider divider_3 (.a(out_4), .b(8'ha), .out({divider_3_out_2, divider_3_out}), .rem(divider_3_rem));  // open: upper
  assign xor_1_out = in_3 ^ {8{in_1}};  // XOR_Gate xor_1, 8 bits wide
  or P1 (P1_out, in_2[0], xor_1_out[0]);
  and G1 (G1_out, in_2[0], xor_1_out[0]);
  or P1_2 (P1_2_out, in_2[1], xor_1_out[1]);
  and G1_2 (G1_2_out, in_2[1], xor_1_out[1]);
  and G2 (G2_out, in_2[2], xor_1_out[2]);
  or P2 (P2_out, in_2[2], xor_1_out[2]);
  and G3 (G3_out, in_2[3], xor_1_out[3]);
  or P3 (P3_out, in_2[3], xor_1_out[3]);
  and G4 (G4_out, in_2[4], xor_1_out[4]);
  or P4 (P4_out, in_2[4], xor_1_out[4]);
  and G5 (G5_out, in_2[5], xor_1_out[5]);
  or P5 (P5_out, in_2[5], xor_1_out[5]);
  and G6 (G6_out, in_2[6], xor_1_out[6]);
  and G7 (G7_out, in_2[7], xor_1_out[7]);
  or P6 (P6_out, in_2[6], xor_1_out[6]);
  or P7 (P7_out, in_2[7], xor_1_out[7]);
  noCout nocout_1 (.S(out_4[0]), .A(in_2[0]), .B(xor_1_out[0]), .C(in_1));
  noCout nocout_2 (.S(out_4[1]), .A(in_2[1]), .B(xor_1_out[1]), .C(or_1_out));
  and and_1 (and_1_out, P1_out, in_1);
  or or_1 (or_1_out, G1_out, and_1_out);
  and and_2 (and_2_out, G1_out, P1_2_out);
  or or_2 (or_2_out, G1_2_out, and_2_out, and_3_out);
  noCout nocout_3 (.S(out_4[2]), .A(in_2[2]), .B(xor_1_out[2]), .C(or_2_out));
  and and_3 (and_3_out, P1_out, P1_2_out, in_1);
  and and_4 (and_4_out, G1_2_out, P2_out);
  or or_3 (or_3_out, G2_out, and_4_out, and_5_out, and_6_out);
  noCout nocout_4 (.S(out_4[3]), .A(in_2[3]), .B(xor_1_out[3]), .C(or_3_out));
  and and_5 (and_5_out, G1_out, P1_2_out, P2_out);
  and and_6 (and_6_out, P1_out, P1_2_out, P2_out, in_1);
  noCout nocout_5 (.S(out_4[4]), .A(in_2[4]), .B(xor_1_out[4]), .C(or_4_out));
  and and_7 (and_7_out, G1_2_out, P2_out, P3_out);
  and and_8 (and_8_out, G2_out, P3_out);
  or or_4 (or_4_out, G3_out, and_8_out, and_7_out, and_9_out, and_10_out);
  and and_9 (and_9_out, G1_out, P1_2_out, P2_out, P3_out);
  and and_10 (and_10_out, P1_out, P1_2_out, P2_out, P3_out, in_1);
  noCout nocout_6 (.S(out_4[5]), .A(in_2[5]), .B(xor_1_out[5]), .C(or_5_out));
  and and_11 (and_11_out, G3_out, P4_out);
  or or_5 (or_5_out, G4_out, and_11_out, and_12_out, and_13_out, and_14_out, and_15_out);
  and and_12 (and_12_out, G2_out, P3_out, P4_out);
  and and_13 (and_13_out, G1_2_out, P2_out, P3_out, P4_out);
  and and_14 (and_14_out, G1_out, P1_2_out, P2_out, P3_out, P4_out);
  and and_15 (and_15_out, P1_out, P1_2_out, P2_out, P3_out, P4_out, in_1);
  noCout nocout_7 (.S(out_4[6]), .A(in_2[6]), .B(xor_1_out[6]), .C(or_6_out));
  and and_16 (and_16_out, G4_out, P5_out);
  or or_6 (or_6_out, G5_out, and_16_out, and_17_out, and_18_out, and_19_out, and_20_out, and_21_out);
  and and_17 (and_17_out, G3_out, P4_out, P5_out);
  and and_18 (and_18_out, G2_out, P3_out, P4_out, P5_out);
  and and_19 (and_19_out, G1_2_out, P2_out, P3_out, P4_out, P5_out);
  and and_20 (and_20_out, G1_out, P1_2_out, P2_out, P3_out, P4_out, P5_out);
  and and_21 (and_21_out, P1_out, P1_2_out, P2_out, P3_out, P4_out, P5_out, in_1);
  noCout nocout_8 (.S(out_4[7]), .A(in_2[7]), .B(xor_1_out[7]), .C(or_7_out));
  and and_22 (and_22_out, G4_out, P5_out, P6_out);
  and and_23 (and_23_out, G5_out, P6_out);
  or or_7 (or_7_out, G6_out, and_23_out, and_22_out, and_24_out, and_25_out, and_26_out, and_27_out, and_28_out);
  and and_24 (and_24_out, G3_out, P4_out, P5_out, P6_out);
  and and_25 (and_25_out, G2_out, P3_out, P4_out, P5_out, P6_out);
  and and_26 (and_26_out, G1_2_out, P2_out, P3_out, P4_out, P5_out, P6_out);
  and and_27 (and_27_out, G1_out, P1_2_out, P2_out, P3_out, P4_out, P5_out, P6_out);
  and and_28 (and_28_out, P1_out, P1_2_out, P2_out, P3_out, P4_out, P5_out, P6_out, in_1);

  assign out_5 = out_4[7];

  // Other names for the same wires on the sheet: MODE = in_1; FIRST[7:0] = in_2; RESULT[7:0] = out_4;
  //   SECOND[7:0] = in_3
endmodule

module Divisor (
  input  [7:0] in_1,
  input  [7:0] in_2,
  output [7:0] out_3,
  output [7:0] out_4
);

  wire _0, _1, _2, _3, _4, _5, _6, _7;
  wire [3:0] divider_1_out, divider_2_out, divider_3_out, divider_4_out;
  wire [7:0] divider_1_rem, divider_2_rem, divider_3_rem, divider_4_rem, multiplexer_1_out,
       multiplexer_3_out, multiplexer_4_out, multiplexer_5_out, multiplexer_6_out, somador_1_out_4,
       somador_2_out_4, somador_3_out_4, somador_4_out_4, somador_5_out_4, somador_6_out_4, somador_7_out_4,
       somador_8_out_4;
  wire [7:1] multiplexer_2_out, multiplexer_7_out_2;
  wire [7:4] divider_1_out_2, divider_2_out_2, divider_3_out_2, divider_4_out_2;
  wire [7:7] multiplexer_2_out_2, multiplexer_7_out;

  not not_1 (out_4[2], _2);
  not not_2 (out_4[4], _4);
  not not_3 (out_4[7], _7);
  not not_4 (out_4[5], _5);
  not not_5 (out_4[3], _3);
  not not_6 (out_4[6], _6);
  Hex_Digit_Display hex_digit_display_1 (.value(divider_1_out));  // open: dp
  Hex_Digit_Display hex_digit_display_2 (.value(divider_2_out));  // open: dp
  not not_7 (out_4[1], _1);
  not not_8 (out_4[0], _0);
  Hex_Digit_Display hex_digit_display_3 (.value(divider_1_rem[3:0]));  // open: dp
  Divider divider_1 (.a(in_1), .b(8'ha), .out({divider_1_out_2, divider_1_out}), .rem(divider_1_rem));  // open: upper
  Hex_Digit_Display hex_digit_display_4 (.value(divider_2_rem[3:0]));  // open: dp
  Divider divider_2 (.a(in_2), .b(8'ha), .out({divider_2_out_2, divider_2_out}), .rem(divider_2_rem));  // open: upper
  Hex_Digit_Display hex_digit_display_5 (.value(divider_3_out));  // open: dp
  Hex_Digit_Display hex_digit_display_6 (.value(divider_4_out));  // open: dp
  Hex_Digit_Display hex_digit_display_7 (.value(divider_3_rem[3:0]));  // open: dp
  Divider divider_3 (.a(out_4), .b(8'ha), .out({divider_3_out_2, divider_3_out}), .rem(divider_3_rem));  // open: upper
  Hex_Digit_Display hex_digit_display_8 (.value(divider_4_rem[3:0]));  // open: dp
  Divider divider_4 (.a(out_3), .b(8'ha), .out({divider_4_out_2, divider_4_out}), .rem(divider_4_rem));  // open: upper
  Somador somador_1 (.in_1(1'b1), .in_2({{7{1'b0}}, in_1[7]}), .in_3(in_2), .out_4(somador_1_out_4), .out_5(_7));
  Multiplexer #(.width(8), .enable("false")) multiplexer_1 (
    .in0(somador_1_out_4), .in1({{7{1'b0}}, in_1[7]}), .out(multiplexer_1_out), .sel(_7));
  Somador somador_2 (
    .in_1(1'b1), .in_2({multiplexer_1_out[6:0], in_1[6]}), .in_3(in_2), .out_4(somador_2_out_4), .out_5(_6));
  Multiplexer #(.width(8), .enable("false")) multiplexer_2 (
    .in0(somador_2_out_4), .in1({multiplexer_1_out[6:0], in_1[6]}),
    .out({multiplexer_2_out_2[7], multiplexer_2_out}), .sel(_6));
  Somador somador_3 (
    .in_1(1'b1), .in_2({multiplexer_2_out, in_1[5]}), .in_3(in_2), .out_4(somador_3_out_4), .out_5(_5));
  Multiplexer #(.width(8), .enable("false")) multiplexer_3 (
    .in0(somador_3_out_4), .in1({multiplexer_2_out, in_1[5]}), .out(multiplexer_3_out), .sel(_5));
  Multiplexer #(.width(8), .enable("false")) multiplexer_4 (
    .in0(somador_4_out_4), .in1({multiplexer_3_out[6:0], in_1[4]}), .out(multiplexer_4_out), .sel(_4));
  Somador somador_4 (
    .in_1(1'b1), .in_2({multiplexer_3_out[6:0], in_1[4]}), .in_3(in_2), .out_4(somador_4_out_4), .out_5(_4));
  Somador somador_5 (
    .in_1(1'b1), .in_2({multiplexer_4_out[6:0], in_1[3]}), .in_3(in_2), .out_4(somador_5_out_4), .out_5(_3));
  Multiplexer #(.width(8), .enable("false")) multiplexer_5 (
    .in0(somador_5_out_4), .in1({multiplexer_4_out[6:0], in_1[3]}), .out(multiplexer_5_out), .sel(_3));
  Multiplexer #(.width(8), .enable("false")) multiplexer_6 (
    .in0(somador_6_out_4), .in1({multiplexer_5_out[6:0], in_1[2]}), .out(multiplexer_6_out), .sel(_2));
  Somador somador_6 (
    .in_1(1'b1), .in_2({multiplexer_5_out[6:0], in_1[2]}), .in_3(in_2), .out_4(somador_6_out_4), .out_5(_2));
  Somador somador_7 (
    .in_1(1'b1), .in_2({multiplexer_6_out[6:0], in_1[1]}), .in_3(in_2), .out_4(somador_7_out_4), .out_5(_1));
  Multiplexer #(.width(8), .enable("false")) multiplexer_7 (
    .in0(somador_7_out_4), .in1({multiplexer_6_out[6:0], in_1[1]}),
    .out({multiplexer_7_out[7], multiplexer_7_out_2}), .sel(_1));
  Multiplexer #(.width(8), .enable("false")) multiplexer_8 (
    .in0(somador_8_out_4), .in1({multiplexer_7_out_2, in_1[0]}), .out(out_3), .sel(_0));
  Somador somador_8 (
    .in_1(1'b1), .in_2({multiplexer_7_out_2, in_1[0]}), .in_3(in_2), .out_4(somador_8_out_4), .out_5(_0));

  // Other names for the same wires on the sheet: DIVIDENDO[7:0] = in_1; DIVISOR[7:0] = in_2; QUOCIENTE[7:0] = out_4;
  //   RESTO[7:0] = out_3
endmodule
