// Logisim project OS NUMEROS.circ as structural Verilog: 3 circuits, main circuit main
module main (
  input  [7:0] Pt_A_B_C_D_E_F_G,
  input  in_2,
  input  in_3,
  input  in_4,
  input  in_5,
  input  in_6,
  input  in_7,
  input  in_8,
  input  in_9,
  input  in_10,
  input  in_11,
  input  [3:0] in_12,
  input  [3:0] in_13,
  input  [3:0] in_14,
  input  [3:0] in_15,
  input  [3:0] in_16,
  input  [3:0] in_17,
  input  [3:0] in_18,
  input  [3:0] in_19,
  input  [3:0] in_20,
  input  [3:0] in_21,
  input  [3:0] in_22
);

  wire ototeste_1_a, ototeste_1_b, ototeste_1_c, ototeste_1_d, ototeste_1_e, ototeste_1_f, ototeste_1_g,
       ototeste_2_a, ototeste_2_b, ototeste_2_c, ototeste_2_d, ototeste_2_e, ototeste_2_f, ototeste_2_g,
       ototeste_3_a, ototeste_3_b, ototeste_3_c, ototeste_3_d, ototeste_3_e, ototeste_3_f, ototeste_3_g,
       ototeste_4_a, ototeste_4_b, ototeste_4_c, ototeste_4_d, ototeste_4_e, ototeste_4_f, ototeste_4_g,
       ototeste_5_a, ototeste_5_b, ototeste_5_c, ototeste_5_d, ototeste_5_e, ototeste_5_f, ototeste_5_g,
       ototeste_6_a, ototeste_6_b, ototeste_6_c, ototeste_6_d, ototeste_6_e, ototeste_6_f, ototeste_6_g,
       ototeste_7_a, ototeste_7_b, ototeste_7_c, ototeste_7_d, ototeste_7_e, ototeste_7_f, ototeste_7_g,
       ototeste_8_a, ototeste_8_b, ototeste_8_c, ototeste_8_d, ototeste_8_e, ototeste_8_f, ototeste_8_g,
       ototeste_9_a, ototeste_9_b, ototeste_9_c, ototeste_9_d, ototeste_9_e, ototeste_9_f, ototeste_9_g,
       ototeste_10_a, ototeste_10_b, ototeste_10_c, ototeste_10_d, ototeste_10_e, ototeste_10_f,
       ototeste_10_g, ototeste_11_a, ototeste_11_b, ototeste_11_c, ototeste_11_d, ototeste_11_e,
       ototeste_11_f, ototeste_11_g, testedrive_1_a, testedrive_1_b, testedrive_1_c, testedrive_1_d,
       testedrive_1_e, testedrive_1_f, testedrive_1_g, testedrive_2_a, testedrive_2_b, testedrive_2_c,
       testedrive_2_d, testedrive_2_e, testedrive_2_f, testedrive_2_g;

  _7_Segment_Display u_7_segment_display_1 (
    .g(testedrive_1_g), .f(testedrive_1_f), .a(testedrive_1_a), .b(testedrive_1_b), .e(testedrive_1_e),
    .d(testedrive_1_d), .c(testedrive_1_c), .dp(in_9));
  testedrive testedrive_1 (
    .in_1({in_5, in_4, in_3, in_2}), .A(testedrive_1_a), .B(testedrive_1_b), .C(testedrive_1_c),
    .D(testedrive_1_d), .E(testedrive_1_e), .F(testedrive_1_f), .G(testedrive_1_g));
  OTOTESTE ototeste_1 (
    .in_1(in_12), .A(ototeste_1_a), .B(ototeste_1_b), .C(ototeste_1_c), .D(ototeste_1_d), .E(ototeste_1_e),
    .F(ototeste_1_f), .G(ototeste_1_g));
  _7_Segment_Display u_7_segment_display_2 (
    .g(ototeste_1_g), .f(ototeste_1_f), .a(ototeste_1_a), .b(ototeste_1_b), .e(ototeste_1_e),
    .d(ototeste_1_d), .c(ototeste_1_c));  // open: dp
  _7_Segment_Display u_7_segment_display_3 (
    .g(ototeste_2_g), .f(ototeste_2_f), .a(ototeste_2_a), .b(ototeste_2_b), .e(ototeste_2_e),
    .d(ototeste_2_d), .c(ototeste_2_c));  // open: dp
  OTOTESTE ototeste_2 (
    .in_1(in_13), .A(ototeste_2_a), .B(ototeste_2_b), .C(ototeste_2_c), .D(ototeste_2_d), .E(ototeste_2_e),
    .F(ototeste_2_f), .G(ototeste_2_g));
  _7_Segment_Display u_7_segment_display_4 (
    .g(testedrive_2_g), .f(testedrive_2_f), .a(testedrive_2_a), .b(testedrive_2_b), .e(testedrive_2_e),
    .d(testedrive_2_d), .c(testedrive_2_c), .dp(in_11));
  OTOTESTE ototeste_3 (
    .in_1(in_14), .A(ototeste_3_a), .B(ototeste_3_b), .C(ototeste_3_c), .D(ototeste_3_d), .E(ototeste_3_e),
    .F(ototeste_3_f), .G(ototeste_3_g));
  _7_Segment_Display u_7_segment_display_5 (
    .g(ototeste_3_g), .f(ototeste_3_f), .a(ototeste_3_a), .b(ototeste_3_b), .e(ototeste_3_e),
    .d(ototeste_3_d), .c(ototeste_3_c));  // open: dp
  _7_Segment_Display u_7_segment_display_6 (
    .g(Pt_A_B_C_D_E_F_G[3]), .f(Pt_A_B_C_D_E_F_G[2]), .a(Pt_A_B_C_D_E_F_G[1]), .b(Pt_A_B_C_D_E_F_G[0]),
    .e(Pt_A_B_C_D_E_F_G[4]), .d(Pt_A_B_C_D_E_F_G[5]), .c(Pt_A_B_C_D_E_F_G[6]), .dp(Pt_A_B_C_D_E_F_G[7]));
  _7_Segment_Display u_7_segment_display_7 (
    .g(ototeste_5_g), .f(ototeste_5_f), .a(ototeste_5_a), .b(ototeste_5_b), .e(ototeste_5_e),
    .d(ototeste_5_d), .c(ototeste_5_c));  // open: dp
  OTOTESTE ototeste_4 (
    .in_1(in_15), .A(ototeste_4_a), .B(ototeste_4_b), .C(ototeste_4_c), .D(ototeste_4_d), .E(ototeste_4_e),
    .F(ototeste_4_f), .G(ototeste_4_g));
  OTOTESTE ototeste_5 (
    .in_1(in_16), .A(ototeste_5_a), .B(ototeste_5_b), .C(ototeste_5_c), .D(ototeste_5_d), .E(ototeste_5_e),
    .F(ototeste_5_f), .G(ototeste_5_g));
  _7_Segment_Display u_7_segment_display_8 (
    .g(ototeste_4_g), .f(ototeste_4_f), .a(ototeste_4_a), .b(ototeste_4_b), .e(ototeste_4_e),
    .d(ototeste_4_d), .c(ototeste_4_c));  // open: dp
  testedrive testedrive_2 (
    .in_1({in_6, in_7, in_8, in_10}), .A(testedrive_2_a), .B(testedrive_2_b), .C(testedrive_2_c),
    .D(testedrive_2_d), .E(testedrive_2_e), .F(testedrive_2_f), .G(testedrive_2_g));
  OTOTESTE ototeste_6 (
    .in_1(in_17), .A(ototeste_6_a), .B(ototeste_6_b), .C(ototeste_6_c), .D(ototeste_6_d), .E(ototeste_6_e),
    .F(ototeste_6_f), .G(ototeste_6_g));
  _7_Segment_Display u_7_segment_display_9 (
    .g(ototeste_6_g), .f(ototeste_6_f), .a(ototeste_6_a), .b(ototeste_6_b), .e(ototeste_6_e),
    .d(ototeste_6_d), .c(ototeste_6_c));  // open: dp
  _7_Segment_Display u_7_segment_display_10 (
    .g(ototeste_7_g), .f(ototeste_7_f), .a(ototeste_7_a), .b(ototeste_7_b), .e(ototeste_7_e),
    .d(ototeste_7_d), .c(ototeste_7_c));  // open: dp
  OTOTESTE ototeste_7 (
    .in_1(in_18), .A(ototeste_7_a), .B(ototeste_7_b), .C(ototeste_7_c), .D(ototeste_7_d), .E(ototeste_7_e),
    .F(ototeste_7_f), .G(ototeste_7_g));
  _7_Segment_Display u_7_segment_display_11 (
    .g(ototeste_8_g), .f(ototeste_8_f), .a(ototeste_8_a), .b(ototeste_8_b), .e(ototeste_8_e),
    .d(ototeste_8_d), .c(ototeste_8_c));  // open: dp
  _7_Segment_Display u_7_segment_display_12 (
    .g(ototeste_9_g), .f(ototeste_9_f), .a(ototeste_9_a), .b(ototeste_9_b), .e(ototeste_9_e),
    .d(ototeste_9_d), .c(ototeste_9_c));  // open: dp
  OTOTESTE ototeste_8 (
    .in_1(in_19), .A(ototeste_8_a), .B(ototeste_8_b), .C(ototeste_8_c), .D(ototeste_8_d), .E(ototeste_8_e),
    .F(ototeste_8_f), .G(ototeste_8_g));
  OTOTESTE ototeste_9 (
    .in_1(in_20), .A(ototeste_9_a), .B(ototeste_9_b), .C(ototeste_9_c), .D(ototeste_9_d), .E(ototeste_9_e),
    .F(ototeste_9_f), .G(ototeste_9_g));
  _7_Segment_Display u_7_segment_display_13 (
    .g(ototeste_10_g), .f(ototeste_10_f), .a(ototeste_10_a), .b(ototeste_10_b), .e(ototeste_10_e),
    .d(ototeste_10_d), .c(ototeste_10_c));  // open: dp
  OTOTESTE ototeste_10 (
    .in_1(in_21), .A(ototeste_10_a), .B(ototeste_10_b), .C(ototeste_10_c), .D(ototeste_10_d),
    .E(ototeste_10_e), .F(ototeste_10_f), .G(ototeste_10_g));
  OTOTESTE ototeste_11 (
    .in_1(in_22), .A(ototeste_11_a), .B(ototeste_11_b), .C(ototeste_11_c), .D(ototeste_11_d),
    .E(ototeste_11_e), .F(ototeste_11_f), .G(ototeste_11_g));
  _7_Segment_Display u_7_segment_display_14 (
    .g(ototeste_11_g), .f(ototeste_11_f), .a(ototeste_11_a), .b(ototeste_11_b), .e(ototeste_11_e),
    .d(ototeste_11_d), .c(ototeste_11_c));  // open: dp
endmodule

module testedrive (
  input  [3:0] in_1,
  output A,
  output B,
  output C,
  output D,
  output E,
  output F,
  output G
);

  wire and_1_out, and_2_out, and_3_out, and_4_out, and_5_out, and_6_out, and_7_out, and_8_out, and_9_out,
       and_10_out, and_11_out, and_12_out, and_13_out, and_14_out, and_15_out, and_16_out, and_17_out,
       and_18_out, and_19_out, and_20_out, and_21_out, and_22_out, and_23_out, and_24_out, and_25_out,
       and_26_out, and_27_out, and_28_out, and_29_out, and_30_out, and_31_out, and_32_out, and_33_out,
       and_34_out, and_35_out, not_1_out, not_2_out, not_3_out, not_4_out, not_5_out, not_6_out, not_7_out,
       not_8_out, not_9_out, not_10_out, not_11_out, not_12_out, not_13_out, not_14_out, not_15_out,
       not_16_out, not_17_out, not_18_out, not_19_out, not_20_out, not_21_out, not_22_out, not_23_out,
       not_24_out, not_25_out, not_26_out, not_27_out, not_28_out, not_29_out, not_30_out, not_31_out,
       not_32_out, not_33_out, not_34_out, not_35_out, not_36_out, not_37_out, not_38_out, not_39_out,
       not_40_out, not_41_out, not_42_out, not_43_out, not_44_out;

  not not_1 (not_1_out, in_1[1]);
  not not_2 (not_2_out, in_1[3]);
  not not_3 (not_3_out, in_1[0]);
  not not_4 (not_4_out, in_1[0]);
  not not_5 (not_5_out, in_1[1]);
  not not_6 (not_6_out, in_1[2]);
  not not_7 (not_7_out, in_1[3]);
  not not_8 (not_8_out, in_1[0]);
  not not_9 (not_9_out, in_1[1]);
  not not_10 (not_10_out, in_1[0]);
  not not_11 (not_11_out, in_1[2]);
  not not_12 (not_12_out, in_1[3]);
  not not_13 (not_13_out, in_1[1]);
  not not_14 (not_14_out, in_1[3]);
  not not_15 (not_15_out, in_1[0]);
  not not_16 (not_16_out, in_1[2]);
  not not_17 (not_17_out, in_1[0]);
  not not_18 (not_18_out, in_1[2]);
  not not_19 (not_19_out, in_1[0]);
  not not_20 (not_20_out, in_1[2]);
  not not_21 (not_21_out, in_1[0]);
  not not_22 (not_22_out, in_1[1]);
  not not_23 (not_23_out, in_1[0]);
  not not_24 (not_24_out, in_1[1]);
  not not_25 (not_25_out, in_1[3]);
  not not_26 (not_26_out, in_1[1]);
  not not_27 (not_27_out, in_1[2]);
  not not_28 (not_28_out, in_1[3]);
  not not_29 (not_29_out, in_1[2]);
  not not_30 (not_30_out, in_1[3]);
  not not_31 (not_31_out, in_1[1]);
  not not_32 (not_32_out, in_1[3]);
  not not_33 (not_33_out, in_1[3]);
  not not_34 (not_34_out, in_1[2]);
  not not_35 (not_35_out, in_1[3]);
  not not_36 (not_36_out, in_1[0]);
  not not_37 (not_37_out, in_1[2]);
  not not_38 (not_38_out, in_1[3]);
  not not_39 (not_39_out, in_1[1]);
  not not_40 (not_40_out, in_1[1]);
  not not_41 (not_41_out, in_1[3]);
  not not_42 (not_42_out, in_1[0]);
  not not_43 (not_43_out, in_1[2]);
  not not_44 (not_44_out, in_1[1]);
  and and_1 (and_1_out, not_1_out, not_2_out);
  and and_2 (and_2_out, not_3_out, in_1[2]);
  and and_3 (and_3_out, not_4_out, in_1[1], in_1[3]);
  and and_4 (and_4_out, in_1[1], in_1[2]);
  and and_5 (and_5_out, in_1[0], not_5_out, not_6_out);
  and and_6 (and_6_out, in_1[0], not_7_out);
  and and_7 (and_7_out, not_8_out, not_9_out);
  and and_8 (and_8_out, not_10_out, not_11_out, not_12_out);
  and and_9 (and_9_out, not_13_out, not_14_out);
  and and_10 (and_10_out, not_15_out, in_1[2], in_1[3]);
  and and_11 (and_11_out, in_1[0], not_16_out, in_1[3]);
  and and_12 (and_12_out, not_17_out, not_18_out);
  and and_13 (and_13_out, not_19_out, in_1[3]);
  and and_14 (and_14_out, not_20_out, in_1[3]);
  and and_15 (and_15_out, not_21_out, in_1[1]);
  and and_16 (and_16_out, in_1[0], not_22_out);
  and and_17 (and_17_out, not_23_out, not_24_out, not_25_out);
  and and_18 (and_18_out, not_26_out, in_1[2], in_1[3]);
  and and_19 (and_19_out, in_1[1], not_27_out, in_1[3]);
  and and_20 (and_20_out, in_1[1], in_1[2], not_28_out);
  and and_21 (and_21_out, in_1[0], not_29_out, not_30_out);
  and and_22 (and_22_out, not_31_out, not_32_out);
  and and_23 (and_23_out, in_1[2], not_33_out);
  and and_24 (and_24_out, in_1[0], in_1[2]);
  and and_25 (and_25_out, in_1[0], in_1[1]);
  and and_26 (and_26_out, not_34_out, not_35_out);
  and and_27 (and_27_out, not_36_out, in_1[1], not_37_out);
  and and_28 (and_28_out, in_1[1], not_38_out);
  and and_29 (and_29_out, in_1[0], not_39_out);
  and and_30 (and_30_out, in_1[0], in_1[2]);
  and and_31 (and_31_out, not_40_out, in_1[2]);
  and and_32 (and_32_out, in_1[2], not_41_out);
  and and_33 (and_33_out, not_42_out, in_1[1], not_43_out);
  and and_34 (and_34_out, in_1[0], not_44_out);
  and and_35 (and_35_out, in_1[0], in_1[3]);
  or or_1 (A, and_1_out, and_2_out, and_3_out, and_4_out, and_5_out, and_6_out);
  or or_2 (B, and_7_out, and_8_out, and_9_out, and_10_out, and_11_out);
  or or_3 (C, and_12_out, and_13_out, and_14_out, and_15_out, and_16_out);
  or or_4 (D, and_17_out, and_18_out, and_19_out, and_20_out, and_21_out);
  or or_5 (E, and_22_out, and_23_out, and_24_out, and_25_out);
  or or_6 (F, and_26_out, and_27_out, and_28_out, and_29_out, and_30_out);
  or or_7 (G, and_31_out, and_32_out, and_33_out, and_34_out, and_35_out);
endmodule

module OTOTESTE (
  input  [3:0] in_1,
  output A,
  output B,
  output C,
  output D,
  output E,
  output F,
  output G
);

  wire and_1_out, and_2_out, and_3_out, and_4_out, and_5_out, and_6_out, and_7_out, and_8_out, and_9_out,
       and_10_out, and_11_out, and_12_out, and_13_out, and_14_out, and_15_out, and_16_out, and_17_out,
       and_18_out, and_19_out, and_20_out, and_21_out, and_22_out, and_23_out, and_24_out, and_25_out,
       and_26_out, and_27_out, and_28_out, and_29_out, and_30_out, and_31_out, and_32_out, and_33_out,
       and_34_out, and_35_out, not_1_out, not_2_out, not_3_out, not_4_out, not_5_out, not_6_out, not_7_out,
       not_8_out, not_9_out, not_10_out, not_11_out, not_12_out, not_13_out, not_14_out, not_15_out,
       not_16_out, not_17_out, not_18_out, not_19_out, not_20_out, not_21_out, not_22_out, not_23_out,
       not_24_out, not_25_out, not_26_out, not_27_out, not_28_out, not_29_out, not_30_out, not_31_out,
       not_32_out, not_33_out, not_34_out, not_35_out, not_36_out, not_37_out, not_38_out, not_39_out,
       not_40_out, not_41_out, not_42_out, not_43_out, not_44_out;

  not not_1 (not_1_out, in_1[1]);
  not not_2 (not_2_out, in_1[3]);
  not not_3 (not_3_out, in_1[0]);
  not not_4 (not_4_out, in_1[0]);
  not not_5 (not_5_out, in_1[1]);
  not not_6 (not_6_out, in_1[2]);
  not not_7 (not_7_out, in_1[3]);
  not not_8 (not_8_out, in_1[0]);
  not not_9 (not_9_out, in_1[1]);
  not not_10 (not_10_out, in_1[0]);
  not not_11 (not_11_out, in_1[2]);
  not not_12 (not_12_out, in_1[3]);
  not not_13 (not_13_out, in_1[1]);
  not not_14 (not_14_out, in_1[3]);
  not not_15 (not_15_out, in_1[0]);
  not not_16 (not_16_out, in_1[2]);
  not not_17 (not_17_out, in_1[0]);
  not not_18 (not_18_out, in_1[2]);
  not not_19 (not_19_out, in_1[0]);
  not not_20 (not_20_out, in_1[2]);
  not not_21 (not_21_out, in_1[0]);
  not not_22 (not_22_out, in_1[1]);
  not not_23 (not_23_out, in_1[0]);
  not not_24 (not_24_out, in_1[1]);
  not not_25 (not_25_out, in_1[3]);
  not not_26 (not_26_out, in_1[1]);
  not not_27 (not_27_out, in_1[2]);
  not not_28 (not_28_out, in_1[3]);
  not not_29 (not_29_out, in_1[2]);
  not not_30 (not_30_out, in_1[3]);
  not not_31 (not_31_out, in_1[1]);
  not not_32 (not_32_out, in_1[3]);
  not not_33 (not_33_out, in_1[3]);
  not not_34 (not_34_out, in_1[2]);
  not not_35 (not_35_out, in_1[3]);
  not not_36 (not_36_out, in_1[0]);
  not not_37 (not_37_out, in_1[2]);
  not not_38 (not_38_out, in_1[3]);
  not not_39 (not_39_out, in_1[1]);
  not not_40 (not_40_out, in_1[1]);
  not not_41 (not_41_out, in_1[3]);
  not not_42 (not_42_out, in_1[0]);
  not not_43 (not_43_out, in_1[2]);
  not not_44 (not_44_out, in_1[1]);
  and and_1 (and_1_out, not_1_out, not_2_out);
  and and_2 (and_2_out, not_3_out, in_1[2]);
  and and_3 (and_3_out, not_4_out, in_1[1], in_1[3]);
  and and_4 (and_4_out, in_1[1], in_1[2]);
  and and_5 (and_5_out, in_1[0], not_5_out, not_6_out);
  and and_6 (and_6_out, in_1[0], not_7_out);
  and and_7 (and_7_out, not_8_out, not_9_out);
  and and_8 (and_8_out, not_10_out, not_11_out, not_12_out);
  and and_9 (and_9_out, not_13_out, not_14_out);
  and and_10 (and_10_out, not_15_out, in_1[2], in_1[3]);
  and and_11 (and_11_out, in_1[0], not_16_out, in_1[3]);
  and and_12 (and_12_out, not_17_out, not_18_out);
  and and_13 (and_13_out, not_19_out, in_1[3]);
  and and_14 (and_14_out, not_20_out, in_1[3]);
  and and_15 (and_15_out, not_21_out, in_1[1]);
  and and_16 (and_16_out, in_1[0], not_22_out);
  and and_17 (and_17_out, not_23_out, not_24_out, not_25_out);
  and and_18 (and_18_out, not_26_out, in_1[2], in_1[3]);
  and and_19 (and_19_out, in_1[1], not_27_out, in_1[3]);
  and and_20 (and_20_out, in_1[1], in_1[2], not_28_out);
  and and_21 (and_21_out, in_1[0], not_29_out, not_30_out);
  and and_22 (and_22_out, not_31_out, not_32_out);
  and and_23 (and_23_out, in_1[2], not_33_out);
  and and_24 (and_24_out, in_1[0], in_1[2]);
  and and_25 (and_25_out, in_1[0], in_1[1]);
  and and_26 (and_26_out, not_34_out, not_35_out);
  and and_27 (and_27_out, not_36_out, in_1[1], not_37_out);
  and and_28 (and_28_out, in_1[1], not_38_out);
  and and_29 (and_29_out, in_1[0], not_39_out);
  and and_30 (and_30_out, in_1[0], in_1[2]);
  and and_31 (and_31_out, not_40_out, in_1[2]);
  and and_32 (and_32_out, in_1[2], not_41_out);
  and and_33 (and_33_out, not_42_out, in_1[1], not_43_out);
  and and_34 (and_34_out, in_1[0], not_44_out);
  and and_35 (and_35_out, in_1[0], in_1[3]);
  or or_1 (A, and_1_out, and_2_out, and_3_out, and_4_out, and_5_out, and_6_out);
  or or_2 (B, and_7_out, and_8_out, and_9_out, and_10_out, and_11_out);
  or or_3 (C, and_12_out, and_13_out, and_14_out, and_15_out, and_16_out);
  or or_4 (D, and_17_out, and_18_out, and_19_out, and_20_out, and_21_out);
  or or_5 (E, and_22_out, and_23_out, and_24_out, and_25_out);
  or or_6 (F, and_26_out, and_27_out, and_28_out, and_29_out, and_30_out);
  or or_7 (G, and_31_out, and_32_out, and_33_out, and_34_out, and_35_out);
endmodule
