// Logisim project RELÓGIO.circ as structural Verilog: 4 circuits, main circuit main
module main (
  input  _1___ON
);

  wire button_1_out, button_2_out, button_3_out, minutos_1_u, segundos_1_u, TURN;
  wire [3:0] horas_1_out_4, horas_1_out_5, minutos_1_out_5, minutos_1_out_6, segundos_1_out_4,
       segundos_1_out_5;

  not not_1 (TURN, _1___ON);
  Button button_1 (.out(button_1_out));
  Hex_Digit_Display hex_digit_display_1 (.value(horas_1_out_5));  // open: dp
  HORAS horas_1 (.in_3(TURN), .out_4(horas_1_out_4), .out_5(horas_1_out_5), .in_1(minutos_1_u), .in_2(button_1_out));
  Hex_Digit_Display hex_digit_display_2 (.value(horas_1_out_4));  // open: dp
  Button button_2 (.out(button_2_out));
  Hex_Digit_Display hex_digit_display_3 (.value(minutos_1_out_6));  // open: dp
  Button button_3 (.out(button_3_out));
  SEGUNDOS segundos_1 (
    .out_4(segundos_1_out_4), .out_5(segundos_1_out_5), .in_2(TURN), .U(segundos_1_u), .in_1(button_3_out));
  MINUTOS minutos_1 (
    .out_5(minutos_1_out_5), .out_6(minutos_1_out_6), .in_1(segundos_1_u), .in_3(TURN), .U(minutos_1_u),
    .in_2(button_2_out));
  Hex_Digit_Display hex_digit_display_4 (.value(minutos_1_out_5));  // open: dp
  Hex_Digit_Display hex_digit_display_5 (.value(segundos_1_out_4));  // open: dp
  Hex_Digit_Display hex_digit_display_6 (.value(segundos_1_out_5));  // open: dp

  // Notes on the sheet:
  //   0 = OFF
  //   :
  //   :
endmodule

module SEGUNDOS (
  input  in_1,
  input  in_2,
  output U,
  output [3:0] out_4,
  output [3:0] out_5
);

  wire and_2_out, clock_1_out, j_k_ff_1_qn, j_k_ff_2_qn, j_k_ff_3_qn, j_k_ff_5_qn, j_k_ff_6_qn, j_k_ff_7_qn,
       or_1_out, or_2_out, or_3_out;

  or or_1 (or_1_out, in_2, U);
  J_K_Flip_Flop j_k_ff_1 (
    .J(1'b1), .clk(or_3_out), .K(1'b1), .Q(out_4[0]), .Qn(j_k_ff_1_qn), .reset(or_1_out));  // open: preset, en
  and and_1 (U, ~out_4[3], out_4[2], out_4[1], ~out_4[0]);  // AND_Gate
  J_K_Flip_Flop j_k_ff_2 (
    .J(1'b1), .clk(j_k_ff_1_qn), .K(1'b1), .Q(out_4[1]), .Qn(j_k_ff_2_qn), .reset(or_1_out));  // open: preset, en
  J_K_Flip_Flop j_k_ff_3 (
    .J(1'b1), .clk(j_k_ff_2_qn), .K(1'b1), .Q(out_4[2]), .Qn(j_k_ff_3_qn), .reset(or_1_out));  // open: preset, en
  J_K_Flip_Flop j_k_ff_4 (
    .J(1'b1), .clk(j_k_ff_3_qn), .K(1'b1), .Q(out_4[3]), .reset(or_1_out));  // open: Qn, preset, en
  Clock clock_1 (.out(clock_1_out));
  or or_2 (or_2_out, in_1, clock_1_out);
  or or_3 (or_3_out, in_2, and_2_out);
  and and_2 (and_2_out, out_5[3], ~out_5[2], out_5[1], ~out_5[0]);  // AND_Gate
  J_K_Flip_Flop j_k_ff_5 (
    .J(1'b1), .clk(or_2_out), .K(1'b1), .Q(out_5[0]), .Qn(j_k_ff_5_qn), .reset(or_3_out));  // open: preset, en
  J_K_Flip_Flop j_k_ff_6 (
    .J(1'b1), .clk(j_k_ff_5_qn), .K(1'b1), .Q(out_5[1]), .Qn(j_k_ff_6_qn), .reset(or_3_out));  // open: preset, en
  J_K_Flip_Flop j_k_ff_7 (
    .J(1'b1), .clk(j_k_ff_6_qn), .K(1'b1), .Q(out_5[2]), .Qn(j_k_ff_7_qn), .reset(or_3_out));  // open: preset, en
  J_K_Flip_Flop j_k_ff_8 (
    .J(1'b1), .clk(j_k_ff_7_qn), .K(1'b1), .Q(out_5[3]), .reset(or_3_out));  // open: Qn, preset, en
endmodule

module MINUTOS (
  input  in_1,
  input  in_2,
  input  in_3,
  output U,
  output [3:0] out_5,
  output [3:0] out_6
);

  wire and_2_out, j_k_ff_1_qn, j_k_ff_2_qn, j_k_ff_3_qn, j_k_ff_5_qn, j_k_ff_6_qn, j_k_ff_7_qn, or_1_out,
       or_2_out, or_3_out;

  or or_1 (or_1_out, in_3, U);
  and and_1 (U, ~out_6[3], out_6[2], out_6[1], ~out_6[0]);  // AND_Gate
  J_K_Flip_Flop j_k_ff_1 (
    .J(1'b1), .clk(or_3_out), .K(1'b1), .Q(out_6[0]), .Qn(j_k_ff_1_qn), .reset(or_1_out));  // open: preset, en
  J_K_Flip_Flop j_k_ff_2 (
    .J(1'b1), .clk(j_k_ff_1_qn), .K(1'b1), .Q(out_6[1]), .Qn(j_k_ff_2_qn), .reset(or_1_out));  // open: preset, en
  J_K_Flip_Flop j_k_ff_3 (
    .J(1'b1), .clk(j_k_ff_2_qn), .K(1'b1), .Q(out_6[2]), .Qn(j_k_ff_3_qn), .reset(or_1_out));  // open: preset, en
  J_K_Flip_Flop j_k_ff_4 (
    .J(1'b1), .clk(j_k_ff_3_qn), .K(1'b1), .Q(out_6[3]), .reset(or_1_out));  // open: Qn, preset, en
  or or_2 (or_2_out, in_2, in_1);
  or or_3 (or_3_out, in_3, and_2_out);
  and and_2 (and_2_out, out_5[3], ~out_5[2], out_5[1], ~out_5[0]);  // AND_Gate
  J_K_Flip_Flop j_k_ff_5 (
    .J(1'b1), .clk(or_2_out), .K(1'b1), .Q(out_5[0]), .Qn(j_k_ff_5_qn), .reset(or_3_out));  // open: preset, en
  J_K_Flip_Flop j_k_ff_6 (
    .J(1'b1), .clk(j_k_ff_5_qn), .K(1'b1), .Q(out_5[1]), .Qn(j_k_ff_6_qn), .reset(or_3_out));  // open: preset, en
  J_K_Flip_Flop j_k_ff_7 (
    .J(1'b1), .clk(j_k_ff_6_qn), .K(1'b1), .Q(out_5[2]), .Qn(j_k_ff_7_qn), .reset(or_3_out));  // open: preset, en
  J_K_Flip_Flop j_k_ff_8 (
    .J(1'b1), .clk(j_k_ff_7_qn), .K(1'b1), .Q(out_5[3]), .reset(or_3_out));  // open: Qn, preset, en
endmodule

module HORAS (
  input  in_1,
  input  in_2,
  input  in_3,
  output [3:0] out_4,
  output [3:0] out_5
);

  wire and_1_out, and_2_out, and_3_out, and_4_out, and_5_out, j_k_ff_1_qn, j_k_ff_2_qn, j_k_ff_3_qn,
       j_k_ff_5_qn, j_k_ff_6_qn, j_k_ff_7_qn, or_1_out, or_2_out, or_3_out;

  or or_1 (or_1_out, in_3, and_2_out, and_1_out);
  and and_1 (and_1_out, ~out_5[3], out_5[2], out_5[1], ~out_5[0]);  // AND_Gate
  Hex_Digit_Display hex_digit_display_1 (.value(out_5));  // open: dp
  J_K_Flip_Flop j_k_ff_1 (
    .J(1'b1), .clk(or_3_out), .K(1'b1), .Q(out_5[0]), .Qn(j_k_ff_1_qn), .reset(or_1_out));  // open: preset, en
  J_K_Flip_Flop j_k_ff_2 (
    .J(1'b1), .clk(j_k_ff_1_qn), .K(1'b1), .Q(out_5[1]), .Qn(j_k_ff_2_qn), .reset(or_1_out));  // open: preset, en
  and and_2 (and_2_out, and_3_out, and_4_out);
  J_K_Flip_Flop j_k_ff_3 (
    .J(1'b1), .clk(j_k_ff_2_qn), .K(1'b1), .Q(out_5[2]), .Qn(j_k_ff_3_qn), .reset(or_1_out));  // open: preset, en
  and and_3 (and_3_out, ~out_5[0], out_5[1], ~out_5[2], ~out_5[3]);  // AND_Gate
  J_K_Flip_Flop j_k_ff_4 (
    .J(1'b1), .clk(j_k_ff_3_qn), .K(1'b1), .Q(out_5[3]), .reset(or_1_out));  // open: Qn, preset, en
  and and_4 (and_4_out, ~out_4[0], ~out_4[1], out_4[2], ~out_4[3]);  // AND_Gate
  or or_2 (or_2_out, in_2, in_1);
  or or_3 (or_3_out, in_3, or_1_out, and_5_out);
  and and_5 (and_5_out, out_4[3], ~out_4[2], out_4[1], ~out_4[0]);  // AND_Gate
  Hex_Digit_Display hex_digit_display_2 (.value(out_4));  // open: dp
  J_K_Flip_Flop j_k_ff_5 (
    .J(1'b1), .clk(or_2_out), .K(1'b1), .Q(out_4[0]), .Qn(j_k_ff_5_qn), .reset(or_3_out));  // open: preset, en
  J_K_Flip_Flop j_k_ff_6 (
    .J(1'b1), .clk(j_k_ff_5_qn), .K(1'b1), .Q(out_4[1]), .Qn(j_k_ff_6_qn), .reset(or_3_out));  // open: preset, en
  J_K_Flip_Flop j_k_ff_7 (
    .J(1'b1), .clk(j_k_ff_6_qn), .K(1'b1), .Q(out_4[2]), .Qn(j_k_ff_7_qn), .reset(or_3_out));  // open: preset, en
  J_K_Flip_Flop j_k_ff_8 (
    .J(1'b1), .clk(j_k_ff_7_qn), .K(1'b1), .Q(out_4[3]), .reset(or_3_out));  // open: Qn, preset, en
endmodule
