// Logisim project SOMADOR MALUCO.circ as structural Verilog
module somador (
  input  A,
  input  B,
  input  C,
  output out_4
);

  wire xor_1_out;

  xor xor_1 (xor_1_out, A, B);
  xor xor_2 (out_4, xor_1_out, C);
endmodule

module lookAhead (
  input  [7:0] in_1,
  input  [7:0] in_2,
  input  in_3,
  output [7:0] out_4
);

  wire G0_out, G1_2_out, G1_3_out, G1_4_out, G1_5_out, G1_6_out, G1_7_out, G1_8_out, G1_9_out, G1_10_out,
       G1_out, G2_out, G3_out, or_1_out, or_2_out, or_3_out, P0_out, P1_out, P2_out, P3_out;

  and G1 (G1_out, G2_out, P3_out);
  or P3 (P3_out, in_2[3], in_1[3]);
  and G1_2 (G1_2_out, G1_8_out, P2_out, P3_out);
  and G1_3 (G1_3_out, G0_out, P1_out, P2_out, P3_out);
  and G3 (G3_out, in_2[3], in_1[3]);
  and G1_4 (G1_4_out, G0_out, P1_out, P2_out, P3_out, in_3);
  or or_1 (or_1_out, G3_out, G1_out, G1_2_out, G1_3_out, G1_4_out);
  somador somador_1 (.C(or_1_out));  // open: A, B, out_4
  or P2 (P2_out, in_2[2], in_1[2]);
  and G2 (G2_out, in_2[2], in_1[2]);
  and G1_5 (G1_5_out, P2_out, G1_8_out);
  or P1 (P1_out, in_2[1], in_1[1]);
  and G1_6 (G1_6_out, G0_out, P1_out, P2_out);
  and G1_7 (G1_7_out, P0_out, P1_out, P2_out, in_3);
  somador somador_2 (.A(in_1[3]), .B(in_2[3]), .C(or_2_out), .out_4(out_4[3]));
  and G1_8 (G1_8_out, in_2[1], in_1[1]);
  or or_2 (or_2_out, G1_5_out, G1_6_out, G1_7_out, G2_out);
  or P0 (P0_out, in_2[0], in_1[0]);
  and G1_9 (G1_9_out, G0_out, P1_out);
  and G0 (G0_out, in_2[0], in_1[0]);
  and G1_10 (G1_10_out, P0_out, P1_out, in_3);
  or or_3 (or_3_out, G1_8_out, G1_9_out, G1_10_out);
  somador somador_3 (.A(in_2[1]), .B(in_1[1]), .C(G0_out), .out_4(out_4[1]));
  somador somador_4 (.A(in_1[2]), .B(in_2[2]), .C(or_3_out), .out_4(out_4[2]));
  somador somador_5 (.A(in_1[0]), .B(in_2[0]), .C(1'b0), .out_4(out_4[0]));
endmodule
