// Logisim project async.circ as structural Verilog: 1 circuit, main circuit main
module main (
);

  wire clock_1_out, clock_2_out, F2_qn;
  wire [3:0] F0_2_q, F0_q;

  Clock clock_1 (.out(clock_1_out));
  Hex_Digit_Display hex_digit_display_1 (.value(F0_q));  // open: dp
  J_K_Flip_Flop F3 (.J(F2_qn), .clk(clock_1_out), .K(1'b1), .Q(F0_q[3]));  // open: Qn, preset, en, reset
  J_K_Flip_Flop F2 (.J(F0_q[3]), .clk(clock_1_out), .K(F0_q[1]), .Q(F0_q[2]), .Qn(F2_qn));  // open: preset, en, reset
  J_K_Flip_Flop F1 (.J(F0_q[2]), .clk(clock_1_out), .K(F2_qn), .Q(F0_q[1]));  // open: Qn, preset, en, reset
  J_K_Flip_Flop F0 (.J(1'b0), .clk(clock_1_out), .K(1'b0), .Q(F0_q[0]));  // open: Qn, preset, en, reset
  Clock clock_2 (.out(clock_2_out));
  Hex_Digit_Display hex_digit_display_2 (.value(F0_2_q));  // open: dp
  J_K_Flip_Flop F3_2 (.J(F0_2_q[2]), .clk(clock_2_out), .K(1'b1), .Q(F0_2_q[3]));  // open: Qn, preset, en, reset
  J_K_Flip_Flop F2_2 (.J(F0_2_q[1]), .clk(clock_2_out), .K(1'b1), .Q(F0_2_q[2]));  // open: Qn, preset, en, reset
  J_K_Flip_Flop F1_2 (.J(F0_2_q[0]), .clk(clock_2_out), .K(1'b1), .Q(F0_2_q[1]));  // open: Qn, preset, en, reset
  J_K_Flip_Flop F0_2 (.J(F0_2_q[3]), .clk(clock_2_out), .K(1'b1), .Q(F0_2_q[0]));  // open: Qn, preset, en, reset
endmodule
